# Fritzing sketch Kran_Sketch (saved by Fritzing 0.9.3b)
breadboards: 1

parts:
  Bauteil1 = Arduino Uno (Rev3)
  R1 = Resistor [tolerance=±5% resistance=10k package=THT]
  R2 = Photocell (LDR) [package=THT]
  C1 = Electrolytic Capacitor [capacitance=100µF package="100 mil [THT, electrolytic]"]
  LED1 = LED - 5mm [color="Red (633nm)" package="5 mm [THT]"]
  J1 = Basic Servo
  LED2 = smd LED [color="Green (555nm)" package="0805 [SMD]"]
  R3 = Resistor [tolerance=±5% resistance=220 package=THT]
  R4 = Resistor [tolerance=±5% resistance=220 package=THT]

nets:
  N1: Bauteil1.A0, R1.Pin_0, R2.pin_1
  N2: Bauteil1.D9_PWM, J1.pulse
  N3: Bauteil1.D2, LED2.anode
  N4: Bauteil1.D3_PWM, LED1.anode
  5V: Bauteil1.5V, R2.pin_0, C1.+, J1.vcc
  GND: Bauteil1.GND, R1.Pin_1, C1.-, J1.gnd, R3.Pin_0, R4.Pin_0
  N5: LED1.cathode, R4.Pin_1
  N6: LED2.cathode, R3.Pin_1
